// Digital circuit CPU.dig as structural Verilog
module CPU (
  input  S,
  input  S_2,
  input  S_3,
  input  S_4,
  input  [7:0] IN,
  input  [7:0] IN_2,
  input  clk
);

  wire and_1_out, and_2_out, and_3_out, cpu_clk_1_p1, cpu_clk_1_p4, cpu_clk_1_p5, cpu_clk_1_p6, undriven_2,
       undriven_3, undriven_4, undriven_5, undriven_6, undriven_8, undriven_9, undriven_10, undriven_11;
  wire [7:0] cpu_clk_1_p2, undriven, undriven_7, undriven_12;

  cpu_temp cpu_temp_1 (.I(undriven_12), .S(and_1_out));  // open: O
  LED led_1 (.in(and_1_out));
  cpu_bus BUS1 (.Bus1(S), .\Ì (undriven));  // open: O
  and and_1 (and_1_out, undriven_5, undriven_6);
  cpu_alu ALU ();
  // cpu_clk cpu_clk_1: pin names not known; wires that end beside it: cpu_clk_1_p1, cpu_clk_1_p2, clk, cpu_clk_1_p4, cpu_clk_1_p5, cpu_clk_1_p6
  LED led_2 (.in(and_2_out));
  cpu_reg_8 ACC (.I(cpu_clk_1_p2), .E(and_2_out));  // open: S, O
  cpu_reg_8 REG0 (.I(IN), .E(1'b1));  // open: S, O
  LED led_3 (.in(undriven_2));
  and and_2 (and_2_out, undriven_2, undriven_4);
  cpu_reg_8 REG1 (.I(IN_2), .E(1'b1));  // open: S, O
  LED led_4 (.in(undriven_5));
  Control control_1 ();
  cpu_reg_8 REG2 (.I(undriven_12), .E(undriven_8));  // open: S, O
  LED led_5 (.in(undriven_10));
  and and_3 (and_3_out, undriven_3, undriven_9);
  cpu_reg_8 REG3 (.I(undriven_12), .E(and_3_out));  // open: S, O
  LED led_6 (.in(and_3_out));
  cpu_ram_256 cpu_ram_256_1 (
    .Address({undriven_12[0], undriven_12[1], undriven_12[2], undriven_12[3], undriven_12[4], undriven_12[5], undriven_12[6], undriven_12[7]}),
    .Reset(undriven_11), .En(1'b0), .I(undriven_7));  // open: Set_adr, Set, O

  // Notes on the sheet:
  //   clk: Hz: 2147483647
endmodule
