// Digital circuit debug.dig as structural Verilog
module debug (
  input  [7:0] IN,
  input  in_2,
  output [7:0] out_3
);

  wire cpu_clk_1_p2, cpu_clk_1_p3, cpu_clk_1_p4, undriven, undriven_3;
  wire [7:0] undriven_2;

  cpu_temp test (.I(undriven_2), .S(undriven));  // open: O
  // cpu_clk cpu_clk_1: pin names not known; wires that end beside it: in_2, cpu_clk_1_p2, cpu_clk_1_p3, cpu_clk_1_p4
  LED led_1 (.in(undriven));
  cpu_reg_8 REG1 (.I(IN), .E(1'b1));  // open: S, O
  LED led_2 (.in(undriven_3));
  Control control_1 ();
  LED led_3 (.in(undriven_3));
endmodule
