// Digital circuit CPU_CONTROL.dig as structural Verilog
module CPU_CONTROL (
  input  CLK,
  input  CLK_E,
  input  CLK_S,
  input  [7:0] IR_IN,
  output ACC_S,
  output MAR_S,
  output RAM_S,
  output TMP_S,
  output R0_S,
  output R1_S,
  output R2_S,
  output R3_S,
  output BUS_1,
  output IR_S,
  output IAR_S,
  output ACC_E,
  output RAM_E,
  output IAR_E,
  output IOCLK_E,
  output R0_E,
  output R1_E,
  output R2_E,
  output R3_E,
  output ALU_0,
  output ALU_1,
  output ALU_2
);

  wire and_5_out, and_6_out, and_7_out, and_8_out, and_9_out, and_10_out, and_11_out, and_12_out, undriven,
       undriven_2, undriven_3, undriven_4, undriven_5, undriven_6, undriven_7, undriven_8, undriven_9;

  or or_1 (R0_E, and_9_out, and_5_out);
  or or_2 (R1_E, and_10_out, and_6_out);
  or or_3 (R2_E, and_11_out, and_7_out);
  or or_4 (R3_E, and_12_out, and_8_out);
  and and_1 (IAR_E, 1'b0, CLK_E);
  and and_2 (RAM_E, 1'b0, CLK_E);
  and and_3 (ACC_E, 1'b0, CLK_E);
  and and_4 (IOCLK_E, 1'b0, CLK_E);
  and and_5 (and_5_out, undriven, CLK_E);
  and and_6 (and_6_out, undriven_2, CLK_E);
  and and_7 (and_7_out, undriven_5, CLK_E);
  and and_8 (and_8_out, undriven_6, CLK_E);
  and and_9 (and_9_out, undriven_3, CLK_E);
  and and_10 (and_10_out, undriven_4, CLK_E);
  and and_11 (and_11_out, undriven_7, CLK_E);
  and and_12 (and_12_out, undriven_8, CLK_E);
  buf and_13 (ALU_0, undriven_9);  // And open: In_1, In_2
  buf and_14 (ALU_1, undriven_9);  // And open: In_1, In_2
  buf and_15 (ALU_2, undriven_9);  // And open: In_1, In_2
  CPU_DECODER_2x4 REG_B ();
  CPU_DECODER_2x4 REG_A ();
  CPU_STEPPER cpu_stepper_1 ();
  // And and_16 is placed but not wired
  buf and_17 (MAR_S, CLK_S);  // And open: In_2
  buf and_18 (ACC_S, CLK_S);  // And open: In_2
  and and_19 (RAM_S, CLK_S, 1'b0);
  and and_20 (TMP_S, CLK_S, 1'b0);
  and and_21 (R0_S, CLK_S, 1'b0);
  and and_22 (R1_S, CLK_S, 1'b0);
  and and_23 (R2_S, CLK_S, 1'b0);
  and and_24 (R3_S, CLK_S, 1'b0);
  buf and_25 (IR_S, CLK_S);  // And open: In_2
  buf and_26 (IAR_S, CLK_S);  // And open: In_2

  // Notes on the sheet:
  //   1
  //   2
  //   3
  //   4
  //   5
  //   6
endmodule
