// Digital circuit CPU_REG_8.dig as structural Verilog
module CPU_REG_8 (
  input  [7:0] I,
  input  S,
  input  E,
  output [7:0] O
);

  wire [7:0] undriven;

  CPU_MEM_8 cpu_mem_8_1 (.I(I), .E(S));  // open: O
  CPU_ENABLE cpu_enable_1 (.I(undriven), .E(E));  // open: O
endmodule
