// Digital circuit CPU_FETCH.dig as structural Verilog
module CPU_FETCH (
  input  RES,
  input  R_0,
  input  R_1,
  input  R_2,
  input  clk,
  input  [7:0] MEM_IN,
  input  in_8,
  input  in_9,
  output [7:0] IR_in
);

  wire cpu_accumulator_1_p2, cpu_accumulator_1_p4, cpu_accumulator_1_p5, cpu_accumulator_1_p7,
       cpu_accumulator_1_p8, IAR_p2, IAR_p3, IAR_p4, IAR_p9, IAR_p10, IAR_p12, IAR_p13, IR_p2, R_0_p2,
       R_0_p3, R_0_p5, R_0_p6, R_0_p8, R_1_p2, R_1_p8, R_1_p11, R_2_p2, R_3_p3, TEMP_p1, TEMP_p2, TEMP_p5;
  wire [7:0] TEMP_p3;

  LED led_1 (.in(TEMP_p2));
  // CPU_MEM_8 TEMP: pin names not known; wires that end beside it: TEMP_p1, TEMP_p2, TEMP_p3, TEMP_p1, TEMP_p5, 1'b0, R_0, R_1, TEMP_p5
  CPU_ALU cpu_alu_1 ();
  CPU_BUS_1 cpu_bus_1_1 (.I(TEMP_p3), .S_1(IAR_p3));  // open: O
  LED led_2 (.in(IAR_p3));
  LED led_3 (.in(cpu_accumulator_1_p4));
  LED led_4 (.in(cpu_accumulator_1_p5));
  // CPU_ACCUMULATOR cpu_accumulator_1: pin names not known; wires that end beside it: R_2, cpu_accumulator_1_p2, cpu_accumulator_1_p2, cpu_accumulator_1_p4, cpu_accumulator_1_p5, TEMP_p1, cpu_accumulator_1_p7, cpu_accumulator_1_p8
  LED led_5 (.in(R_0_p2));
  LED led_6 (.in(R_0_p3));
  // CPU_REGISTER_8 R_0: pin names not known; wires that end beside it: TEMP_p1, R_0_p2, R_0_p3, clk, R_0_p5, R_0_p6, TEMP_p1, R_0_p8
  CPU_CLK cpu_clk_1 ();
  LED led_7 (.in(R_1_p2));
  LED led_8 (.in(cpu_accumulator_1_p7));
  // CPU_REGISTER_8 R_1: pin names not known; wires that end beside it: TEMP_p1, R_1_p2, cpu_accumulator_1_p7, R_0_p6, R_0_p8, R_0_p5, cpu_accumulator_1_p5, R_1_p8, R_0_p3, TEMP_p1, R_1_p11
  CPU_CONTROL cpu_control_1 ();
  LED led_9 (.in(R_2_p2));
  LED led_10 (.in(IAR_p10));
  // CPU_REGISTER_8 R_2: pin names not known; wires that end beside it: TEMP_p1, R_2_p2, cpu_accumulator_1_p8, TEMP_p1
  LED led_11 (.in(cpu_accumulator_1_p8));
  RESET1 reset1_1 (.Set_1(in_8), .Line_in(R_1_p11));  // open: Line_out
  LED led_12 (.in(IAR_p12));
  // CPU_REGISTER_8 IAR: pin names not known; wires that end beside it: cpu_accumulator_1_p4, IAR_p2, IAR_p3, IAR_p4, R_2_p2, R_1_p2, R_0_p2, TEMP_p2, IAR_p9, IAR_p10, TEMP_p1, IAR_p12, IAR_p13
  LED led_13 (.in(IAR_p4));
  // CPU_MEM_8 IR: pin names not known; wires that end beside it: TEMP_p1, IR_p2, IR_in
  // RESET reset_1: pin names not known; wires that end beside it: in_9, TEMP_p1, IAR_p13
  // CPU_REGISTER_8 R_3: pin names not known; wires that end beside it: TEMP_p1, IAR_p4, R_3_p3, TEMP_p1
  LED led_14 (.in(R_3_p3));
  LED led_15 (.in(IR_p2));
  // CPU_RAM_256 cpu_ram_256_1: pin names not known; wires that end beside it: IAR_p12, IAR_p2, TEMP_p1, MEM_IN, RES, TEMP_p1, R_1_p8, IAR_p9

  // Notes on the sheet:
  //   clk: Hz: 2147483647
endmodule
